# Fritzing sketch 1D_Ping_Pong_v1.7_Wiring Schematics (saved by Fritzing 0.9.3b)

parts:
  Part1 = Arduino Uno (Rev3) - ICSP
  P1_TM1637 = Grove 4 Digit Display
  P2_TM1637 = Grove 4 Digit Display
  P2_Power = Round Pushbutton
  P1_Hit = Round Pushbutton
  P1_Power = Round Pushbutton
  P2_Hit = Round Pushbutton
  RGB = WS2812 RGB LED strip
  Buzzer = Piezo Speaker
  25v_1000uf = Capacitor Polarized [package=cpol-radial-1000uf-25v]
  part = Resistor [tolerance=±5% resistance=320 package=THT]

nets:
  GND: Part1.GND, P1_TM1637.GND, P2_Power.leg1, P1_Hit.leg0, P1_Power.leg1, P2_Hit.leg1, RGB.GND, Buzzer.pin1, 25v_1000uf.-
  N1: Part1.D8, P1_TM1637.CLK
  N2: Part1.D9_PWM, P1_TM1637.DIO
  N3: Part1.D10_PWM/SS, P2_TM1637.CLK
  N4: Part1.D11_PWM/MOSI, P2_TM1637.DIO
  N5: Part1.D2, part.Pin_1
  N6: Part1.D3_PWM, Buzzer.pin2
  N7: Part1.D4, P1_Hit.leg1
  N8: Part1.D5_PWM, P1_Power.leg0
  N9: Part1.D6_PWM, P2_Power.leg0
  N10: Part1.D7, P2_Hit.leg0
  5V: Part1.5V, RGB.VCC, 25v_1000uf.+
  VCC: P1_TM1637.VCC, P2_TM1637.VCC
  N11: RGB.DIN, part.Pin_0

custom parts:
  WS2812 RGB LED strip: WS2812 strip
